// Logisim project logisimdatapath.circ as structural Verilog: 7 circuits, main circuit main
module pc (
  input  [31:0] next_pc,
  input  clk,
  input  reset,
  output [31:0] pc
);

  Register #(.width(32)) u_PC (.D(next_pc), .Q(pc), .clk(clk), .clr(reset));  // open: en

  // Notes on the sheet:
  //   PC register
endmodule

module main (
  input  RegWEn,
  input  PCSel,
  input  ASel,
  input  reset,
  input  [1:0] WBSel,
  input  BSel,
  input  [2:0] ALUSel,
  input  [1:0] ImmSel,
  output [31:0] pc,
  output [31:0] alu_result,
  output BrEq,
  output BrLT,
  output [31:0] inst,
  output [31:0] wb
);

  wire clock_1_out, clock_2_out;
  wire [31:0] adder_1_out, imm_gen_1_imm, multiplexer_1_out, multiplexer_2_out, multiplexer_3_out,
       register_file_1_dataa, register_file_1_datab;

  Multiplexer #(.width(32), .enable("false")) multiplexer_1 (
    .in0(adder_1_out), .in1(alu_result), .out(multiplexer_1_out), .sel(PCSel));
  pc pc_1 (.next_pc(multiplexer_1_out), .pc(pc), .clk(clock_1_out), .reset(reset));
  Clock clock_1 (.out(clock_1_out));
  Adder #(.width(32)) adder_1 (.a(pc), .b(32'h4), .out(adder_1_out));  // open: cin, cout
  instruction_memory instruction_memory_1 (.addr(pc), .inst(inst));
  register_file register_file_1 (
    .AddrA(inst[19:15]), .AddrB(inst[24:20]), .AddrD(inst[11:7]), .DataD(wb), .RegWEn(RegWEn),
    .clk(clock_2_out), .DataA(register_file_1_dataa), .DataB(register_file_1_datab));
  imm_gen imm_gen_1 (.inst(inst), .ImmSel(ImmSel), .Imm(imm_gen_1_imm));
  Clock clock_2 (.out(clock_2_out));
  branch_comp branch_comp_1 (.DataA(register_file_1_dataa), .DataB(register_file_1_datab), .BrEq(BrEq), .BrLT(BrLT));
  Multiplexer #(.width(32), .enable("false")) multiplexer_2 (
    .in0(register_file_1_dataa), .in1(pc), .out(multiplexer_2_out), .sel(ASel));
  Multiplexer #(.width(32), .enable("false")) multiplexer_3 (
    .in0(register_file_1_datab), .in1(imm_gen_1_imm), .out(multiplexer_3_out), .sel(BSel));
  alu alu_1 (.A(multiplexer_2_out), .B(multiplexer_3_out), .ALUSel(ALUSel), .result(alu_result));
  Multiplexer #(.select(2), .width(32), .enable("false")) multiplexer_4 (
    .in0({32{1'b0}}), .in1(alu_result), .in2(adder_1_out), .in3({32{1'b0}}), .out(wb), .sel(WBSel));

  // Notes on the sheet:
  //   PC mux
  //   +4
  //   inst[19:15]
  //   inst[24:20]
  //   inst[11:7]
  //   ASel mux
  //   BSel mux
  //   mem (reserved)
  //   WB mux
endmodule

module instruction_memory (
  input  [31:0] addr,
  output [31:0] inst
);

  wire comparator_1_eq;
  wire [31:0] rom_1_data;

  Comparator #(.width(24), .mode("unsigned")) comparator_1 (
    .a(addr[31:8]), .b({24{1'b0}}), .eq(comparator_1_eq));  // open: gt, lt
  ROM #(.addrWidth(6), .dataWidth(32)) rom_1 (.addr(addr[7:2]), .data(rom_1_data));  // open: sel
  Multiplexer #(.width(32), .enable("false")) multiplexer_1 (
    .in0({32{1'b0}}), .in1(rom_1_data), .out(inst), .sel(comparator_1_eq));

  // Notes on the sheet:
  //   addr[7:2]
  //   addr[31:8] == 0 ?
  //   contents of rom_1 (hex, n*v repeats v):
  //   700293 500313 6283b3 40628433 38463 8384b3
endmodule

module imm_gen (
  input  [31:0] inst,
  input  [1:0] ImmSel,
  output [31:0] Imm
);

  wire [31:0] bit_extender_1_out, bit_extender_2_out, bit_extender_3_out;

  assign bit_extender_1_out = {{20{inst[31]}}, inst[31:20]};  // Bit_Extender bit_extender_1
  assign bit_extender_2_out = {{20{inst[31]}}, {inst[31:25], inst[11:7]}};  // Bit_Extender bit_extender_2
  assign bit_extender_3_out = {{19{inst[31]}}, {inst[31], inst[7], inst[30:25], inst[11:8], 1'b0}};  // Bit_Extender bit_extender_3
  Multiplexer #(.select(2), .width(32), .enable("false")) multiplexer_1 (
    .in0(bit_extender_1_out), .in1(bit_extender_2_out), .in2(bit_extender_3_out), .in3({32{1'b0}}),
    .out(Imm), .sel(ImmSel));

  // Notes on the sheet:
  //   I: inst[31:20]
  //   S: inst[31:25], inst[11:7]
  //   B: inst[31], inst[7], inst[30:25], inst[11:8], 0
endmodule

module register_file (
  input  [31:0] DataD,
  input  clk,
  input  RegWEn,
  input  [4:0] AddrD,
  input  [4:0] AddrA,
  input  [4:0] AddrB,
  output [31:0] DataA,
  output [31:0] DataB
);

  wire decoder_1_out1, decoder_1_out2, decoder_1_out3, decoder_1_out4, decoder_1_out5, decoder_1_out6,
       decoder_1_out7, decoder_1_out8, decoder_1_out9, decoder_1_out10, decoder_1_out11, decoder_1_out12,
       decoder_1_out13, decoder_1_out14, decoder_1_out15, decoder_1_out16, decoder_1_out17, decoder_1_out18,
       decoder_1_out19, decoder_1_out20, decoder_1_out21, decoder_1_out22, decoder_1_out23, decoder_1_out24,
       decoder_1_out25, decoder_1_out26, decoder_1_out27, decoder_1_out28, decoder_1_out29, decoder_1_out30,
       decoder_1_out31;
  wire [31:0] x1_q, x2_q, x3_q, x4_q, x5_q, x6_q, x7_q, x8_q, x9_q, x10_q, x11_q, x12_q, x13_q, x14_q, x15_q,
       x16_q, x17_q, x18_q, x19_q, x20_q, x21_q, x22_q, x23_q, x24_q, x25_q, x26_q, x27_q, x28_q, x29_q,
       x30_q, x31_q;

  Decoder #(.select(5), .disabled(0)) decoder_1 (
    .out1(decoder_1_out1), .out2(decoder_1_out2), .out3(decoder_1_out3), .out4(decoder_1_out4),
    .out5(decoder_1_out5), .out6(decoder_1_out6), .out7(decoder_1_out7), .out8(decoder_1_out8),
    .out9(decoder_1_out9), .out10(decoder_1_out10), .out11(decoder_1_out11), .out12(decoder_1_out12),
    .out13(decoder_1_out13), .out14(decoder_1_out14), .out15(decoder_1_out15), .out16(decoder_1_out16),
    .out17(decoder_1_out17), .out18(decoder_1_out18), .out19(decoder_1_out19), .out20(decoder_1_out20),
    .out21(decoder_1_out21), .out22(decoder_1_out22), .out23(decoder_1_out23), .out24(decoder_1_out24),
    .out25(decoder_1_out25), .out26(decoder_1_out26), .out27(decoder_1_out27), .out28(decoder_1_out28),
    .out29(decoder_1_out29), .out30(decoder_1_out30), .out31(decoder_1_out31), .sel(AddrD), .en(RegWEn));  // open: out0
  Register #(.width(32)) x1 (.D(DataD), .en(decoder_1_out1), .Q(x1_q), .clk(clk));  // open: clr
  Register #(.width(32)) x2 (.D(DataD), .en(decoder_1_out2), .Q(x2_q), .clk(clk));  // open: clr
  Register #(.width(32)) x3 (.D(DataD), .en(decoder_1_out3), .Q(x3_q), .clk(clk));  // open: clr
  Register #(.width(32)) x4 (.D(DataD), .en(decoder_1_out4), .Q(x4_q), .clk(clk));  // open: clr
  Register #(.width(32)) x5 (.D(DataD), .en(decoder_1_out5), .Q(x5_q), .clk(clk));  // open: clr
  Register #(.width(32)) x6 (.D(DataD), .en(decoder_1_out6), .Q(x6_q), .clk(clk));  // open: clr
  Register #(.width(32)) x7 (.D(DataD), .en(decoder_1_out7), .Q(x7_q), .clk(clk));  // open: clr
  Register #(.width(32)) x8 (.D(DataD), .en(decoder_1_out8), .Q(x8_q), .clk(clk));  // open: clr
  Register #(.width(32)) x9 (.D(DataD), .en(decoder_1_out9), .Q(x9_q), .clk(clk));  // open: clr
  Register #(.width(32)) x10 (.D(DataD), .en(decoder_1_out10), .Q(x10_q), .clk(clk));  // open: clr
  Register #(.width(32)) x11 (.D(DataD), .en(decoder_1_out11), .Q(x11_q), .clk(clk));  // open: clr
  Register #(.width(32)) x12 (.D(DataD), .en(decoder_1_out12), .Q(x12_q), .clk(clk));  // open: clr
  Register #(.width(32)) x13 (.D(DataD), .en(decoder_1_out13), .Q(x13_q), .clk(clk));  // open: clr
  Register #(.width(32)) x14 (.D(DataD), .en(decoder_1_out14), .Q(x14_q), .clk(clk));  // open: clr
  Register #(.width(32)) x15 (.D(DataD), .en(decoder_1_out15), .Q(x15_q), .clk(clk));  // open: clr
  Register #(.width(32)) x16 (.D(DataD), .en(decoder_1_out16), .Q(x16_q), .clk(clk));  // open: clr
  Register #(.width(32)) x17 (.D(DataD), .en(decoder_1_out17), .Q(x17_q), .clk(clk));  // open: clr
  Register #(.width(32)) x18 (.D(DataD), .en(decoder_1_out18), .Q(x18_q), .clk(clk));  // open: clr
  Register #(.width(32)) x19 (.D(DataD), .en(decoder_1_out19), .Q(x19_q), .clk(clk));  // open: clr
  Register #(.width(32)) x20 (.D(DataD), .en(decoder_1_out20), .Q(x20_q), .clk(clk));  // open: clr
  Register #(.width(32)) x21 (.D(DataD), .en(decoder_1_out21), .Q(x21_q), .clk(clk));  // open: clr
  Register #(.width(32)) x22 (.D(DataD), .en(decoder_1_out22), .Q(x22_q), .clk(clk));  // open: clr
  Register #(.width(32)) x23 (.D(DataD), .en(decoder_1_out23), .Q(x23_q), .clk(clk));  // open: clr
  Register #(.width(32)) x24 (.D(DataD), .en(decoder_1_out24), .Q(x24_q), .clk(clk));  // open: clr
  Register #(.width(32)) x25 (.D(DataD), .en(decoder_1_out25), .Q(x25_q), .clk(clk));  // open: clr
  Register #(.width(32)) x26 (.D(DataD), .en(decoder_1_out26), .Q(x26_q), .clk(clk));  // open: clr
  Register #(.width(32)) x27 (.D(DataD), .en(decoder_1_out27), .Q(x27_q), .clk(clk));  // open: clr
  Register #(.width(32)) x28 (.D(DataD), .en(decoder_1_out28), .Q(x28_q), .clk(clk));  // open: clr
  Register #(.width(32)) x29 (.D(DataD), .en(decoder_1_out29), .Q(x29_q), .clk(clk));  // open: clr
  Register #(.width(32)) x30 (.D(DataD), .en(decoder_1_out30), .Q(x30_q), .clk(clk));  // open: clr
  Register #(.width(32)) x31 (.D(DataD), .en(decoder_1_out31), .Q(x31_q), .clk(clk));  // open: clr
  Multiplexer #(.select(5), .width(32), .enable("false")) multiplexer_1 (
    .in0({32{1'b0}}), .in1(x1_q), .in2(x2_q), .in3(x3_q), .in4(x4_q), .in5(x5_q), .in6(x6_q), .in7(x7_q),
    .in8(x8_q), .in9(x9_q), .in10(x10_q), .in11(x11_q), .in12(x12_q), .in13(x13_q), .in14(x14_q),
    .in15(x15_q), .in16(x16_q), .in17(x17_q), .in18(x18_q), .in19(x19_q), .in20(x20_q), .in21(x21_q),
    .in22(x22_q), .in23(x23_q), .in24(x24_q), .in25(x25_q), .in26(x26_q), .in27(x27_q), .in28(x28_q),
    .in29(x29_q), .in30(x30_q), .in31(x31_q), .out(DataA), .sel(AddrA));
  Multiplexer #(.select(5), .width(32), .enable("false")) multiplexer_2 (
    .in0({32{1'b0}}), .in1(x1_q), .in2(x2_q), .in3(x3_q), .in4(x4_q), .in5(x5_q), .in6(x6_q), .in7(x7_q),
    .in8(x8_q), .in9(x9_q), .in10(x10_q), .in11(x11_q), .in12(x12_q), .in13(x13_q), .in14(x14_q),
    .in15(x15_q), .in16(x16_q), .in17(x17_q), .in18(x18_q), .in19(x19_q), .in20(x20_q), .in21(x21_q),
    .in22(x22_q), .in23(x23_q), .in24(x24_q), .in25(x25_q), .in26(x26_q), .in27(x27_q), .in28(x28_q),
    .in29(x29_q), .in30(x30_q), .in31(x31_q), .out(DataB), .sel(AddrB));

  // Notes on the sheet:
  //   write select
  //   32 x 32-bit register file (x0 = 0)
  //   x0 = 0
  //   read port A
  //   read port B
endmodule

module branch_comp (
  input  [31:0] DataA,
  input  [31:0] DataB,
  output BrEq,
  output BrLT
);

  Comparator #(.width(32)) comparator_1 (.a(DataA), .b(DataB), .eq(BrEq), .lt(BrLT));  // open: gt
endmodule

module alu (
  input  [31:0] A,
  input  [31:0] B,
  input  [2:0] ALUSel,
  output [31:0] result
);

  wire comparator_1_lt;
  wire [31:0] adder_1_out, and_1_out, bit_extender_1_out, or_1_out, subtractor_1_out, xor_1_out;

  Adder #(.width(32)) adder_1 (.a(A), .b(B), .out(adder_1_out));  // open: cin, cout
  Subtractor #(.width(32)) subtractor_1 (.a(A), .b(B), .out(subtractor_1_out));  // open: bin, bout
  assign and_1_out = A & B;  // AND_Gate and_1, 32 bits wide
  assign or_1_out = A | B;  // OR_Gate or_1, 32 bits wide
  assign xor_1_out = A ^ B;  // XOR_Gate xor_1, 32 bits wide
  Comparator #(.width(32)) comparator_1 (.a(A), .b(B), .lt(comparator_1_lt));  // open: gt, eq
  assign bit_extender_1_out = {{31{1'b0}}, comparator_1_lt};  // Bit_Extender bit_extender_1
  Multiplexer #(.select(3), .width(32), .enable("false")) multiplexer_1 (
    .in0(and_1_out), .in1(or_1_out), .in2(adder_1_out), .in3(xor_1_out), .in4({32{1'b0}}), .in5({32{1'b0}}),
    .in6(subtractor_1_out), .in7(bit_extender_1_out), .out(result), .sel(ALUSel));

  // Notes on the sheet:
  //   ADD
  //   SUB
  //   AND
  //   OR
  //   XOR
  //   SLT
  //   ALUSel: 000 AND, 001 OR, 010 ADD, 011 XOR, 110 SUB, 111 SLT
endmodule
