// Logisim project 32bit_PC_IM.circ as structural Verilog: 1 circuit, main circuit main
module main (
  input  in_1,
  output [31:0] PC,
  output [31:0] instruction
);

  wire clock_1_out;
  wire [31:0] adder_1_out;

  Clock clock_1 (.out(clock_1_out));
  Register #(.width(32)) u_PC (.D(adder_1_out), .Q(PC), .clk(clock_1_out), .clr(in_1));  // open: en
  Adder #(.width(32)) adder_1 (.a(PC), .b(32'h4), .out(adder_1_out));  // open: cin, cout
  ROM #(.addrWidth(4), .dataWidth(32)) rom_1 (.addr(PC[5:2]), .data(instruction));  // open: sel

  // Notes on the sheet:
  //   contents of rom_1 (hex, n*v repeats v):
  //   10093 200113 3081b3 400013 500213 600293 700313 800393 900413 a00493 b00513 c00593 d00613 e00693
  //   f00713 1000793
endmodule
