// Logisim project Register_File_4bit.circ as structural Verilog: 1 circuit, main circuit main
module main (
  input  [3:0] in_1,
  input  [1:0] rd1,
  input  [1:0] rd2,
  output [3:0] dataout1,
  output [3:0] dataout2
);

  wire clock_1_out, decoder_1_out0, decoder_1_out1, decoder_1_out2, decoder_1_out3;
  wire [3:0] r1_q, r2_q, r3_q, r4_q;

  Clock clock_1 (.out(clock_1_out));
  Decoder #(.select(2), .enable("false")) decoder_1 (
    .out0(decoder_1_out0), .out1(decoder_1_out1), .out2(decoder_1_out2), .out3(decoder_1_out3));  // open: sel
  Register #(.width(4)) r1 (.D(in_1), .en(decoder_1_out0), .Q(r1_q), .clk(clock_1_out));  // open: clr
  Register #(.width(4)) r2 (.D(in_1), .en(decoder_1_out1), .Q(r2_q), .clk(clock_1_out));  // open: clr
  Register #(.width(4)) r3 (.D(in_1), .en(decoder_1_out2), .Q(r3_q), .clk(clock_1_out));  // open: clr
  Register #(.width(4)) r4 (.D(in_1), .en(decoder_1_out3), .Q(r4_q), .clk(clock_1_out));  // open: clr
  Multiplexer #(.select(2), .width(4), .enable("false")) multiplexer_1 (
    .in0(r1_q), .in1(r2_q), .in2(r3_q), .in3(r4_q), .out(dataout1), .sel(rd1));
  Multiplexer #(.select(2), .width(4), .enable("false")) multiplexer_2 (
    .in0(r1_q), .in1(r2_q), .in2(r3_q), .in3(r4_q), .out(dataout2), .sel(rd2));
endmodule
